# Fritzing sketch ESP32 GPIO Schematic (saved by Fritzing 0.9.3b)
breadboards: 1

parts:
  MH-ET_LIVE_ESP32_DEVKIT2 = MH-ET LIVE ESP32 DEVKIT 38 pins
  R1 = Resistor [tolerance=±5% resistance=220 package=THT]
  LED1 = LED - 5mm [color="Red (633nm)" package="5 mm [THT]"]
  S1 = Pushbutton [package="[THT]"]

nets:
  N1: MH-ET_LIVE_ESP32_DEVKIT2.3V3, LED1.anode
  N2: MH-ET_LIVE_ESP32_DEVKIT2.GND, S1.Pin_1, S1.Pin_2
  N3: MH-ET_LIVE_ESP32_DEVKIT2.IO17, S1.Pin_3, S1.Pin_4
  N4: MH-ET_LIVE_ESP32_DEVKIT2.IO16, R1.Pin_1
  N5: R1.Pin_0, LED1.cathode

custom parts:
  MH-ET LIVE ESP32 DEVKIT 38 pins: http://mh.nodebb.com/topic/2/mh-et-live-esp32-devkit
