# Fritzing sketch ESP32 ADC Schematic (saved by Fritzing 0.9.3b)
breadboards: 1

parts:
  MH-ET_LIVE_ESP32_DEVKIT2 = MH-ET LIVE ESP32 DEVKIT 38 pins
  U1 = POT [package=pot_mammoth]

nets:
  N1: MH-ET_LIVE_ESP32_DEVKIT2.3V3, U1.S
  N2: MH-ET_LIVE_ESP32_DEVKIT2.IO34, U1.A
  N3: MH-ET_LIVE_ESP32_DEVKIT2.GND, U1.E

custom parts:
  MH-ET LIVE ESP32 DEVKIT 38 pins: http://mh.nodebb.com/topic/2/mh-et-live-esp32-devkit
