# Fritzing sketch ESP32 PWM Schematic (saved by Fritzing 0.9.3b)
breadboards: 1

parts:
  MH-ET_LIVE_ESP32_DEVKIT2 = MH-ET LIVE ESP32 DEVKIT 38 pins
  R1 = Resistor [tolerance=±5% resistance=220 package=THT]
  LED1 = LED - 5mm [color="Red (633nm)" package="5 mm [THT]"]

nets:
  N1: MH-ET_LIVE_ESP32_DEVKIT2.GND, LED1.cathode
  N2: MH-ET_LIVE_ESP32_DEVKIT2.IO16, R1.Pin_0
  N3: R1.Pin_1, LED1.anode

custom parts:
  MH-ET LIVE ESP32 DEVKIT 38 pins: http://mh.nodebb.com/topic/2/mh-et-live-esp32-devkit
