# Fritzing sketch ESP32 Touch Wake Up Schematic (saved by Fritzing 0.9.3b)

parts:
  J1 = STARBOARD_GND [package=starboard_ground_small]
  MH-ET_LIVE_ESP32_DEVKIT2 = MH-ET LIVE ESP32 DEVKIT 38 pins

nets:
  N1: J1.MOUNT, MH-ET_LIVE_ESP32_DEVKIT2.IO4

custom parts:
  MH-ET LIVE ESP32 DEVKIT 38 pins: http://mh.nodebb.com/topic/2/mh-et-live-esp32-devkit
