# Fritzing sketch ESP32 EXT Wake Up Schematic (saved by Fritzing 0.9.3b)
breadboards: 1

parts:
  MH-ET_LIVE_ESP32_DEVKIT2 = MH-ET LIVE ESP32 DEVKIT 38 pins
  S1 = Pushbutton [package="[THT]"]
  R1 = Resistor [tolerance=±5% resistance=220 package=THT]

nets:
  N1: MH-ET_LIVE_ESP32_DEVKIT2.3V3, S1.Pin_3, S1.Pin_4
  N2: MH-ET_LIVE_ESP32_DEVKIT2.IO33, S1.Pin_1, S1.Pin_2, R1.Pin_0
  N3: MH-ET_LIVE_ESP32_DEVKIT2.GND, R1.Pin_1

custom parts:
  MH-ET LIVE ESP32 DEVKIT 38 pins: http://mh.nodebb.com/topic/2/mh-et-live-esp32-devkit
