# Fritzing sketch ESP32 webserver wifi station Schematic (saved by Fritzing 0.9.3b)
breadboards: 1

parts:
  MH-ET_LIVE_ESP32_DEVKIT2 = MH-ET LIVE ESP32 DEVKIT 38 pins
  R1 = Resistor [tolerance=±5% resistance=220 package=THT]
  LED1 = LED - 5mm [color="Red (633nm)" package="5 mm [THT]"]
  R2 = Resistor [tolerance=±5% resistance=220 package=THT]
  LED2 = LED - 5mm [color="Red (633nm)" package="5 mm [THT]"]

nets:
  N1: MH-ET_LIVE_ESP32_DEVKIT2.3V3, R1.Pin_1, R2.Pin_1
  N2: MH-ET_LIVE_ESP32_DEVKIT2.IO26, LED1.cathode
  N3: MH-ET_LIVE_ESP32_DEVKIT2.IO27, LED2.cathode
  N4: R1.Pin_0, LED1.anode
  N5: R2.Pin_0, LED2.anode

custom parts:
  MH-ET LIVE ESP32 DEVKIT 38 pins: http://mh.nodebb.com/topic/2/mh-et-live-esp32-devkit
